// Logisim project logic_circuit_experiment.circ as structural Verilog
module \実験1  (
  input  A0,
  input  A1,
  input  A2,
  input  A3
);

  Hex_Digit_Display hex_digit_display_1 (.value({A3, A2, A1, A0}));  // open: dp

  // Notes on the sheet:
  //   26002103701 Mitsuishi Kaito
endmodule

// Half Adder
module \実験3  (
  input  A,
  input  B,
  output C,
  output S
);

  and and_1 (C, A, B);
  xor xor_1 (S, A, B);

  // Notes on the sheet:
  //   26002103701 Mitsuishi Kaito
endmodule

// Full Adder
module \実験4  (
  input  A,
  input  B,
  input  C,
  output C_prime,
  output S
);

  wire \実験3_1_c , \実験3_1_s , \実験3_2_c ;

  \実験3  \u_実験3_1  (.A(A), .C(\実験3_1_c ), .B(B), .S(\実験3_1_s ));
  \実験3  \u_実験3_2  (.A(\実験3_1_s ), .C(\実験3_2_c ), .B(C), .S(S));
  or or_1 (C_prime, \実験3_1_c , \実験3_2_c );

  // Notes on the sheet:
  //   26002103701 Mitsuishi Kaito
  //   A
  //   B
  //   C
  //   S
  //   A
  //   B
  //   C
  //   S
endmodule

module \実験5  (
  input  A,
  input  B,
  input  A_2,
  input  B_2,
  input  C,
  output C_2,
  output S,
  output C_prime,
  output S_2
);

  wire nand_1_out, nand_2_out, nand_3_out, nand_4_out, nand_5_out, nand_6_out, nand_8_out, nand_9_out,
       nand_12_out, nand_13_out;

  nand nand_1 (nand_1_out, A, B);
  nand nand_2 (nand_2_out, A_2, B_2);
  nand nand_3 (nand_3_out, A, nand_1_out);
  nand nand_4 (nand_4_out, nand_1_out, B);
  nand nand_5 (nand_5_out, A_2, nand_2_out);
  nand nand_6 (nand_6_out, nand_2_out, B_2);
  nand nand_7 (C_2, nand_1_out, nand_1_out);
  nand nand_8 (nand_8_out, nand_5_out, nand_6_out);
  nand nand_9 (nand_9_out, nand_8_out, C);
  nand nand_10 (S, nand_3_out, nand_4_out);
  nand nand_11 (C_prime, nand_2_out, nand_9_out);
  nand nand_12 (nand_12_out, nand_8_out, nand_9_out);
  nand nand_13 (nand_13_out, nand_9_out, C);
  nand nand_14 (S_2, nand_12_out, nand_13_out);

  // Notes on the sheet:
  //   Half Adder
  //   26002103701 Mitsuishi Kaito
  //   Full Adder
endmodule

module \実験6  (
  input  A_0,
  input  A_1,
  input  A_2,
  input  A_3,
  input  A_4,
  input  A_5,
  input  A_6,
  output Q_2,
  output Q_1,
  output Q_0
);

  wire \実験4_1_c_prime , \実験4_1_s , \実験4_3_c_prime , \実験4_3_s , \実験4_4_c_prime ;

  \実験4  \u_実験4_1  (.A(A_0), .B(A_1), .C(A_2), .C_prime(\実験4_1_c_prime ), .S(\実験4_1_s ));
  \実験4  \u_実験4_2  (.A(\実験4_1_c_prime ), .B(\実験4_3_c_prime ), .C(\実験4_4_c_prime ), .C_prime(Q_2), .S(Q_1));
  \実験4  \u_実験4_3  (.A(A_3), .B(A_4), .C(A_5), .C_prime(\実験4_3_c_prime ), .S(\実験4_3_s ));
  \実験4  \u_実験4_4  (.A(\実験4_1_s ), .B(\実験4_3_s ), .C(A_6), .C_prime(\実験4_4_c_prime ), .S(Q_0));

  // Notes on the sheet:
  //   26002103701 Mitsuishi Kaito
endmodule

// 4-bit sequential carry adder
module \実験7  (
  input  y_3,
  input  x_3,
  input  y_2,
  input  x_2,
  input  y_1,
  input  x_1,
  input  y_0,
  input  x_0,
  output O_F,
  output z_3,
  output z_2,
  output z_1,
  output z_0
);

  wire \実験3_1_c , \実験4_2_c_prime , \実験4_3_c_prime ;

  \実験4  \u_実験4_1  (.A(y_3), .B(x_3), .C(\実験4_2_c_prime ), .C_prime(O_F), .S(z_3));
  \実験4  \u_実験4_2  (.A(y_2), .B(x_2), .C(\実験4_3_c_prime ), .C_prime(\実験4_2_c_prime ), .S(z_2));
  \実験4  \u_実験4_3  (.A(y_1), .B(x_1), .C(\実験3_1_c ), .C_prime(\実験4_3_c_prime ), .S(z_1));
  \実験3  \u_実験3_1  (.A(x_0), .C(\実験3_1_c ), .B(y_0), .S(z_0));

  // Notes on the sheet:
  //   26002103701 Mitsuishi Kaito
  //   B
  //   S
  //   A
  //   C
endmodule

// 4-bit sign inverter
module \実験9  (
  input  a_3,
  input  a_2,
  input  a_1,
  input  a_0,
  output O_F,
  output b_2,
  output b_3,
  output b_1,
  output b_0
);

  wire not_1_out, not_2_out, not_3_out, not_4_out;

  not not_1 (not_1_out, a_3);
  \実験7  \u_実験7_1  (
    .y_3(not_1_out), .x_3(1'b0), .y_2(not_2_out), .x_2(1'b0), .y_1(not_3_out), .x_1(1'b0), .y_0(not_4_out),
    .x_0(1'b1), .O_F(O_F), .z_3(b_3), .z_2(b_2), .z_1(b_1), .z_0(b_0));
  not not_2 (not_2_out, a_2);
  not not_3 (not_3_out, a_1);
  not not_4 (not_4_out, a_0);

  // Notes on the sheet:
  //   26002103701 Mitsuishi Kaito
endmodule

// 4-bit parallel subtractor
module \実験10  (
  input  s_3,
  input  s_2,
  input  s_1,
  input  s_0,
  input  t_3,
  input  t_2,
  input  t_1,
  input  t_0,
  output O_F__1,
  output O_F__2,
  output u_3,
  output u_2,
  output u_1,
  output u_0
);

  wire \実験9_1_b_0 , \実験9_1_b_1 , \実験9_1_b_2 , \実験9_1_b_3 ;

  \実験9  \u_実験9_1  (
    .a_3(s_3), .a_1(s_1), .a_0(s_0), .O_F(O_F__1), .b_3(\実験9_1_b_3 ), .b_2(\実験9_1_b_2 ), .b_1(\実験9_1_b_1 ),
    .b_0(\実験9_1_b_0 ), .a_2(s_2));
  \実験7  \u_実験7_1  (
    .y_3(\実験9_1_b_3 ), .x_3(t_3), .y_2(\実験9_1_b_2 ), .x_2(t_2), .y_1(\実験9_1_b_1 ), .x_1(t_1),
    .y_0(\実験9_1_b_0 ), .x_0(t_0), .O_F(O_F__2), .z_3(u_3), .z_2(u_2), .z_1(u_1), .z_0(u_0));

  // Notes on the sheet:
  //   26002103701 Mitsuishi Kaito
endmodule

// 4-bit parallel subtractor
module \実験11  (
  input  a_3,
  input  a_2,
  input  a_1,
  input  a_0,
  input  b_3,
  input  b_2,
  input  b_1,
  input  b_0,
  output O_F__1,
  output _0_F__2,
  output Result
);

  wire \実験10_1_u_0 , \実験10_1_u_1 , \実験10_1_u_2 , \実験10_1_u_3 ;

  \実験10  \u_実験10_1  (
    .s_3(a_3), .s_2(a_2), .s_1(a_1), .s_0(a_0), .t_3(b_3), .t_2(b_2), .t_1(b_1), .t_0(b_0), .O_F__1(O_F__1),
    .O_F__2(_0_F__2), .u_3(\実験10_1_u_3 ), .u_2(\実験10_1_u_2 ), .u_1(\実験10_1_u_1 ), .u_0(\実験10_1_u_0 ));
  nor nor_1 (Result, \実験10_1_u_3 , \実験10_1_u_2 , \実験10_1_u_1 , \実験10_1_u_0 );

  // Notes on the sheet:
  //   26002103701 Mitsuishi Kaito
endmodule

module \実験12  (
  input  S,
  input  R,
  output Q,
  output Q_prime
);

  wire not_1_out, not_2_out;

  not not_1 (not_1_out, S);
  not not_2 (not_2_out, R);
  nand nand_1 (Q, not_1_out, Q_prime);
  nand nand_2 (Q_prime, Q, not_2_out);

  // Notes on the sheet:
  //   26002103701 Mitsuishi Kaito
endmodule

module SR_F_F (
  input  Set,
  input  S,
  input  CLK,
  input  R,
  input  Reset,
  output Q,
  output Q_prime
);

  wire nand_1_out, nand_2_out, not_1_out, not_2_out;

  not not_1 (not_1_out, Set);
  nand nand_1 (nand_1_out, S, CLK);
  nand nand_2 (nand_2_out, CLK, R);
  not not_2 (not_2_out, Reset);
  nand nand_3 (Q, not_1_out, nand_1_out, Q_prime);
  nand nand_4 (Q_prime, Q, nand_2_out, not_2_out);

  // Notes on the sheet:
  //   26002103701 Mitsuishi Kaito
endmodule

module \実験13  (
  input  Set,
  input  J,
  input  CLK,
  input  K,
  input  Reset,
  output Q,
  output Q_prime
);

  wire and_1_out, and_2_out;

  and and_1 (and_1_out, Q_prime, J);
  and and_2 (and_2_out, K, Q);
  SR_F_F sr_f_f_1 (.S(and_1_out), .CLK(CLK), .R(and_2_out), .Q(Q), .Q_prime(Q_prime), .Set(Set), .Reset(Reset));

  // Notes on the sheet:
  //   26002103701 Mitsuishi Kaito
endmodule

// JK-F.F.
module \実験14  (
  input  Set,
  input  J,
  input  K,
  input  CLK,
  input  Reset,
  output Q,
  output Q_prime
);

  wire nand_1_out, nand_2_out, nand_3_out, nand_4_out, nand_5_out, nand_6_out, not_1_out, not_2_out,
       not_3_out;

  not not_1 (not_1_out, Set);
  nand nand_1 (nand_1_out, J, Q_prime, CLK);
  nand nand_2 (nand_2_out, CLK, Q, K);
  not not_2 (not_2_out, Reset);
  nand nand_3 (nand_3_out, not_1_out, nand_1_out, nand_4_out);
  nand nand_4 (nand_4_out, nand_3_out, nand_2_out, not_2_out);
  not not_3 (not_3_out, CLK);
  nand nand_5 (nand_5_out, nand_3_out, not_3_out);
  nand nand_6 (nand_6_out, not_3_out, nand_4_out);
  nand nand_7 (Q, not_1_out, Q_prime, nand_5_out);
  nand nand_8 (Q_prime, nand_6_out, Q, not_2_out);

  // Notes on the sheet:
  //   26002103701 Mitsuishi Kaito
endmodule

// D-F.F.
module \実験15  (
  input  Set,
  input  D,
  input  CLK,
  input  Reset,
  output Q,
  output Q_prime
);

  wire not_1_out;

  not not_1 (not_1_out, D);
  \実験14  \u_実験14_1  (.J(D), .K(not_1_out), .CLK(CLK), .Q(Q), .Q_prime(Q_prime), .Set(Set), .Reset(Reset));

  // Notes on the sheet:
  //   26002103701 Mitsuishi Kaito
endmodule

// Selecter
module _2_bit_selecter (
  input  Select,
  input  X0,
  input  X1,
  output Y
);

  wire and_1_out, and_2_out, not_1_out;

  and and_1 (and_1_out, X0, not_1_out);
  not not_1 (not_1_out, Select);
  and and_2 (and_2_out, X1, Select);
  or or_1 (Y, and_1_out, and_2_out);

  // Notes on the sheet:
  //   26002103701 Mitsuishi Kaito
endmodule

// 4bit sift regester
module \実験16  (
  input  D3,
  input  D2,
  input  D1,
  input  D0,
  input  Set,
  input  Select,
  input  D,
  input  Reset,
  input  CLK,
  output Q3,
  output Q2,
  output Q1,
  output Q0
);

  wire n2_bit_selecter_1_y, n2_bit_selecter_2_y, n2_bit_selecter_3_y, n2_bit_selecter_4_y;

  _2_bit_selecter u_2_bit_selecter_1 (.X0(D), .X1(D3), .Y(n2_bit_selecter_1_y), .Select(Select));
  \実験15  \u_実験15_1  (.D(n2_bit_selecter_1_y), .CLK(CLK), .Q(Q3), .Set(Set), .Reset(Reset));  // open: Q_prime
  _2_bit_selecter u_2_bit_selecter_2 (.X0(Q3), .X1(D2), .Y(n2_bit_selecter_2_y), .Select(Select));
  \実験15  \u_実験15_2  (.D(n2_bit_selecter_2_y), .CLK(CLK), .Q(Q2), .Set(Set), .Reset(Reset));  // open: Q_prime
  _2_bit_selecter u_2_bit_selecter_3 (.X0(Q2), .X1(D1), .Y(n2_bit_selecter_3_y), .Select(Select));
  \実験15  \u_実験15_3  (.D(n2_bit_selecter_3_y), .CLK(CLK), .Q(Q1), .Set(Set), .Reset(Reset));  // open: Q_prime
  _2_bit_selecter u_2_bit_selecter_4 (.X0(Q1), .X1(D0), .Y(n2_bit_selecter_4_y), .Select(Select));
  \実験15  \u_実験15_4  (.D(n2_bit_selecter_4_y), .CLK(CLK), .Q(Q0), .Set(Set), .Reset(Reset));  // open: Q_prime

  // Notes on the sheet:
  //   26002103701 Mitsuishi Kaito
endmodule

module \実験17  (
  input  a_0,
  input  a_1,
  input  a_2,
  input  a_3,
  input  D,
  input  b_0,
  input  b_1,
  input  b_2,
  input  b_3,
  input  CLK,
  input  Select,
  input  Set,
  input  Reset
);

  wire \実験4_1_c_prime , \実験4_1_s , \実験15_1_q ;
  wire [3:0] \実験16_1_q0 , \実験16_2_q0 ;

  \実験16  \u_実験16_1  (
    .Set(Set), .Select(Select), .D(\実験4_1_s ), .Reset(Reset), .CLK(CLK), .D3(a_0), .D2(a_1), .D1(a_2),
    .D0(a_3), .Q3(\実験16_1_q0 [3]), .Q2(\実験16_1_q0 [2]), .Q1(\実験16_1_q0 [1]), .Q0(\実験16_1_q0 [0]));
  \実験16  \u_実験16_2  (
    .Set(Set), .Select(Select), .D(D), .Reset(Reset), .CLK(CLK), .D3(b_0), .D2(b_1), .D1(b_2), .D0(b_3),
    .Q3(\実験16_2_q0 [3]), .Q2(\実験16_2_q0 [2]), .Q1(\実験16_2_q0 [1]), .Q0(\実験16_2_q0 [0]));
  \実験4  \u_実験4_1  (.A(\実験16_1_q0 [0]), .B(\実験16_2_q0 [0]), .C(\実験15_1_q ), .C_prime(\実験4_1_c_prime ), .S(\実験4_1_s ));
  \実験15  \u_実験15_1  (.D(\実験4_1_c_prime ), .CLK(CLK), .Q(\実験15_1_q ), .Set(Set), .Reset(Reset));  // open: Q_prime
  Hex_Digit_Display hex_digit_display_1 (.value(\実験16_1_q0 ));  // open: dp
  Hex_Digit_Display hex_digit_display_2 (.value(\実験16_2_q0 ));  // open: dp

  // Notes on the sheet:
  //   26002103701 Mitsuishi Kaito
endmodule

module \実験18  (
  input  X_0,
  input  X_1,
  input  Y_0,
  input  Y_1,
  output Z_0,
  output Z_1,
  output Z_2,
  output Z_3
);

  wire and_2_out, and_3_out, and_4_out, \実験3_1_c ;

  and and_1 (Z_0, X_0, Y_0);
  and and_2 (and_2_out, X_1, Y_0);
  and and_3 (and_3_out, X_0, Y_1);
  and and_4 (and_4_out, X_1, Y_1);
  \実験3  \u_実験3_1  (.A(and_2_out), .C(\実験3_1_c ), .B(and_3_out), .S(Z_1));
  \実験3  \u_実験3_2  (.A(\実験3_1_c ), .C(Z_3), .B(and_4_out), .S(Z_2));

  // Notes on the sheet:
  //   26002103701 Mitsuishi Kaito
endmodule
